// Logisim project LogismDiagrams.circ as structural Verilog: 1 circuit, main circuit main
module main (
  input  in_1,
  input  in_2,
  input  in_3,
  input  in_4,
  output out_5,
  output out_6
);

  wire and_1_out, and_2_out, nand_1_out, nand_2_out, not_1_out, not_2_out;

  not not_1 (not_1_out, in_1);
  not not_2 (not_2_out, in_4);
  and and_1 (and_1_out, not_1_out, in_4);
  and and_2 (and_2_out, in_1, not_2_out);
  or or_1 (out_5, and_1_out, and_2_out);
  nand nand_1 (nand_1_out, in_2, in_2, in_2);
  nand nand_2 (nand_2_out, in_3, in_3);
  nand nand_3 (out_6, nand_1_out, nand_2_out);

  // Notes on the sheet:
  //   My first XOR
  //   OR
endmodule
